// Logisim project WITCPU.circ as structural Verilog: 1 circuit, main circuit main
module main (
  input  [15:0] DATA,
  input  [3:0] Rx,
  input  in_3,
  input  [3:0] RD,
  input  [3:0] Ry,
  output [15:0] out_6,
  output [15:0] out_7
);

  wire demultiplexer_1_out0, demultiplexer_1_out1, demultiplexer_1_out2, demultiplexer_1_out3,
       demultiplexer_1_out4, demultiplexer_1_out5, demultiplexer_1_out6, demultiplexer_1_out7,
       demultiplexer_1_out8, demultiplexer_1_out9, demultiplexer_1_out10, demultiplexer_1_out11,
       demultiplexer_1_out12, demultiplexer_1_out13, demultiplexer_1_out14, demultiplexer_1_out15;
  wire [15:0] R0_q, Rc_q, Rd_q, Re_q, Rf_q;

  Demultiplexer #(.select(4)) demultiplexer_1 (
    .out0(demultiplexer_1_out0), .out1(demultiplexer_1_out1), .out2(demultiplexer_1_out2),
    .out3(demultiplexer_1_out3), .out4(demultiplexer_1_out4), .out5(demultiplexer_1_out5),
    .out6(demultiplexer_1_out6), .out7(demultiplexer_1_out7), .out8(demultiplexer_1_out8),
    .out9(demultiplexer_1_out9), .out10(demultiplexer_1_out10), .out11(demultiplexer_1_out11),
    .out12(demultiplexer_1_out12), .out13(demultiplexer_1_out13), .out14(demultiplexer_1_out14),
    .out15(demultiplexer_1_out15), .in(in_3), .sel(RD));  // open: en
  Register #(.width(16)) R0 (.D(DATA), .Q(R0_q), .clk(demultiplexer_1_out0));  // open: en, clr
  Register #(.width(16)) R1 (.D(DATA), .Q(R0_q), .clk(demultiplexer_1_out3));  // open: en, clr
  Register #(.width(16)) R2 (.D(DATA), .Q(R0_q), .clk(demultiplexer_1_out6));  // open: en, clr
  Register #(.width(16)) R3 (.D(DATA), .Q(R0_q), .clk(demultiplexer_1_out9));  // open: en, clr
  Register #(.width(16)) R4 (.D(DATA), .Q(R0_q), .clk(demultiplexer_1_out12));  // open: en, clr
  Register #(.width(16)) R5 (.D(DATA), .Q(R0_q), .clk(demultiplexer_1_out1));  // open: en, clr
  Register #(.width(16)) R6 (.D(DATA), .Q(R0_q), .clk(demultiplexer_1_out4));  // open: en, clr
  Register #(.width(16)) R7 (.D(DATA), .Q(R0_q), .clk(demultiplexer_1_out7));  // open: en, clr
  Register #(.width(16)) R8 (.D(DATA), .Q(R0_q), .clk(demultiplexer_1_out10));  // open: en, clr
  Register #(.width(16)) R9 (.D(DATA), .Q(R0_q), .clk(demultiplexer_1_out13));  // open: en, clr
  Register #(.width(16)) Ra (.D(DATA), .Q(R0_q), .clk(demultiplexer_1_out2));  // open: en, clr
  Register #(.width(16)) Rb (.D(DATA), .Q(R0_q), .clk(demultiplexer_1_out5));  // open: en, clr
  Register #(.width(16)) Rc (.D(DATA), .Q(Rc_q), .clk(demultiplexer_1_out8));  // open: en, clr
  Register #(.width(16)) u_Rd (.D(DATA), .Q(Rd_q), .clk(demultiplexer_1_out11));  // open: en, clr
  Register #(.width(16)) Re (.D(DATA), .Q(Re_q), .clk(demultiplexer_1_out14));  // open: en, clr
  Register #(.width(16)) Rf (.D(DATA), .Q(Rf_q), .clk(demultiplexer_1_out15));  // open: en, clr
  Multiplexer #(.select(4)) multiplexer_1 (
    .in0(R0_q[0]), .in1(R0_q[0]), .in2(R0_q[0]), .in3(R0_q[0]), .in4(R0_q[0]), .in5(R0_q[0]), .in6(R0_q[0]),
    .in7(R0_q[0]), .in8(R0_q[0]), .in9(R0_q[0]), .in10(R0_q[0]), .in11(R0_q[0]), .in12(Rc_q[0]),
    .in13(Rd_q[0]), .in14(Re_q[0]), .in15(Rf_q[0]), .out(out_6[0]), .sel(Rx));  // open: en
  Multiplexer #(.select(4)) multiplexer_2 (
    .in0(R0_q[0]), .in1(R0_q[0]), .in2(R0_q[0]), .in3(R0_q[0]), .in4(R0_q[0]), .in5(R0_q[0]), .in6(R0_q[0]),
    .in7(R0_q[0]), .in8(R0_q[0]), .in9(R0_q[0]), .in10(R0_q[0]), .in11(R0_q[0]), .in12(Rc_q[0]),
    .in13(Rd_q[0]), .in14(Re_q[0]), .in15(Rf_q[0]), .out(out_7[0]), .sel(Ry));  // open: en
  // Pins of 1 and 16 bits meet at Rf_q
  // Pins of 1 and 16 bits meet at R0_q
  // Pins of 1 and 16 bits meet at Rc_q
  // Pins of 1 and 16 bits meet at Rd_q
  // Pins of 1 and 16 bits meet at Re_q
  // Pins of 1 and 16 bits meet at out_6
  // Pins of 1 and 16 bits meet at out_7
endmodule
